// Logisim project Clock_Logiscm.circ as structural Verilog: 19 circuits, main circuit hoursmincounter
module L_3_bit_adder_2dd98d25 (
  input  in_1,
  input  in_2,
  input  in_3,
  output out_4,
  output out_5,
  output out_6
);

  wire and_1_out, j_k_ff_1_qn, j_k_ff_2_qn, not_1_out, or_1_out;

  J_K_Flip_Flop j_k_ff_1 (
    .J(in_1), .K(in_1), .clk(in_3), .Q(out_4), .Qn(j_k_ff_1_qn), .reset(or_1_out));  // open: preset
  J_K_Flip_Flop j_k_ff_2 (
    .J(in_1), .K(in_1), .clk(j_k_ff_1_qn), .Q(out_5), .Qn(j_k_ff_2_qn), .reset(or_1_out));  // open: preset
  not not_1 (not_1_out, out_4);
  J_K_Flip_Flop j_k_ff_3 (.J(in_1), .K(in_1), .clk(j_k_ff_2_qn), .Q(out_6), .reset(or_1_out));  // open: Qn, preset
  and and_1 (and_1_out, out_6, out_5, not_1_out);
  or or_1 (or_1_out, and_1_out, in_2);
endmodule

module L_4bitreset_c5035a69 (
  input  Enable,
  input  Clk,
  input  in_3,
  output B0,
  output b1,
  output B2,
  output B3,
  output Co
);

  wire and_1_out, and_2_out, and_3_out, and_5_out, and_6_out, and_7_out, not_1_out, or_1_out;

  and and_1 (and_1_out, Enable, B0);
  and and_2 (and_2_out, and_1_out, b1);
  and and_3 (and_3_out, and_2_out, B2);
  J_K_Flip_Flop j_k_ff_1 (.J(Enable), .K(Enable), .clk(Clk), .Q(B0), .reset(or_1_out));  // open: Qn, preset
  J_K_Flip_Flop j_k_ff_2 (.J(and_1_out), .K(and_1_out), .clk(Clk), .Q(b1), .reset(or_1_out));  // open: Qn, preset
  J_K_Flip_Flop j_k_ff_3 (.J(and_2_out), .K(and_2_out), .clk(Clk), .Q(B2), .reset(or_1_out));  // open: Qn, preset
  J_K_Flip_Flop j_k_ff_4 (.J(and_3_out), .K(and_3_out), .clk(Clk), .Q(B3), .reset(or_1_out));  // open: Qn, preset
  and and_4 (Co, B3, and_3_out);
  or or_1 (or_1_out, and_7_out, in_3);
  and and_5 (and_5_out, B0, B2);
  and and_6 (and_6_out, b1, B3);
  not not_1 (not_1_out, and_5_out);
  and and_7 (and_7_out, not_1_out, and_6_out);
endmodule

module hoursmincounter (
  input  in_1,
  output [3:0] out_2,
  output [3:0] out_3,
  output [3:0] out_4,
  output [3:0] out_5
);

  wire and_1_out, and_2_out, and_3_out, and_4_out, and_5_out, and_6_out, and_7_out, clock_1_out, not_1_out,
       not_2_out, not_3_out, not_4_out;

  and and_1 (and_1_out, and_4_out, and_2_out);
  twobitmodthree twobitmodthree_1 (
    .in_1(and_7_out), .in_3(clock_1_out), .in_2(and_1_out), .out_4(out_4[0]), .out_5(out_4[1]));
  and and_2 (and_2_out, out_2[0], out_2[3]);
  L_4bitreset_c5035a69 l_4bitreset_c5035a69_1 (
    .Enable(and_4_out), .Clk(clock_1_out), .in_3(and_7_out), .B2(out_2[2]), .b1(out_2[1]), .B3(out_2[3]),
    .B0(out_2[0]));  // open: Co
  and and_3 (and_3_out, out_3[0], out_3[2]);
  and and_4 (and_4_out, and_3_out, and_6_out);
  L_3_bit_adder_2dd98d25 l_3_bit_adder_2dd98d25_1 (
    .in_2(and_7_out), .in_3(and_5_out), .in_1(clock_1_out), .out_6(out_3[2]), .out_4(out_3[0]),
    .out_5(out_3[1]));
  and and_5 (and_5_out, not_1_out, not_2_out, not_3_out, not_4_out);
  and and_6 (and_6_out, out_5[3], out_5[0]);
  and and_7 (and_7_out, out_2[2], out_4[1]);
  L_4bitreset_c5035a69 l_4bitreset_c5035a69_2 (
    .Enable(in_1), .Clk(clock_1_out), .in_3(and_7_out), .B2(out_5[2]), .b1(out_5[1]), .B3(out_5[3]),
    .B0(out_5[0]));  // open: Co
  not not_1 (not_1_out, out_5[3]);
  not not_2 (not_2_out, out_5[2]);
  not not_3 (not_3_out, out_5[1]);
  not not_4 (not_4_out, out_5[0]);
  Clock clock_1 (.out(clock_1_out));

  assign out_3[3] = 1'b0;
  assign out_4[3:2] = 2'b00;
endmodule

module sevenseg (
  input  [3:0] in_1,
  output [6:0] out_2
);

  sega sega_1 (.b0(in_1[3]), .b1(in_1[2]), .b2(in_1[1]), .b3(in_1[0]), .a(out_2[0]));
  segb segb_1 (.b0(in_1[3]), .b1(in_1[2]), .b2(in_1[1]), .b3(in_1[0]), .b(out_2[1]));
  segc segc_1 (.b0(in_1[3]), .b1(in_1[2]), .b2(in_1[1]), .b3(in_1[0]), .c(out_2[2]));
  segd segd_1 (.b0(in_1[3]), .b1(in_1[2]), .b2(in_1[1]), .b3(in_1[0]), .d(out_2[3]));
  sege sege_1 (.b0(in_1[3]), .b1(in_1[2]), .b2(in_1[1]), .b3(in_1[0]), .e(out_2[4]));
  segf segf_1 (.b0(in_1[3]), .b1(in_1[2]), .b2(in_1[1]), .b3(in_1[0]), .f(out_2[5]));
  segg segg_1 (.b0(in_1[3]), .b1(in_1[2]), .b2(in_1[1]), .b3(in_1[0]), .g(out_2[6]));
endmodule

module sega (
  input  b0,
  input  b1,
  input  b2,
  input  b3,
  output a
);

  wire and_1_out, and_2_out, and_3_out, and_4_out, and_5_out, and_6_out, not_1_out, not_2_out, not_3_out,
       not_4_out, not_5_out, not_6_out, not_7_out;

  not not_1 (not_1_out, b1);
  not not_2 (not_2_out, b3);
  not not_3 (not_3_out, b0);
  not not_4 (not_4_out, b0);
  not not_5 (not_5_out, b1);
  not not_6 (not_6_out, b2);
  not not_7 (not_7_out, b3);
  and and_1 (and_1_out, not_1_out, not_2_out);
  and and_2 (and_2_out, not_3_out, b2);
  and and_3 (and_3_out, not_4_out, b1, b3);
  and and_4 (and_4_out, b1, b2);
  and and_5 (and_5_out, b0, not_5_out, not_6_out);
  and and_6 (and_6_out, b0, not_7_out);
  or or_1 (a, and_1_out, and_2_out, and_3_out, and_4_out, and_5_out, and_6_out);
endmodule

module segb (
  input  b0,
  input  b1,
  input  b2,
  input  b3,
  output b
);

  wire and_1_out, and_2_out, and_3_out, and_4_out, and_5_out, and_6_out, not_1_out, not_2_out, not_3_out,
       not_4_out, not_5_out, not_6_out, not_7_out, not_8_out, not_9_out, not_10_out, not_11_out;

  not not_1 (not_1_out, b0);
  not not_2 (not_2_out, b1);
  not not_3 (not_3_out, b0);
  not not_4 (not_4_out, b2);
  not not_5 (not_5_out, b3);
  not not_6 (not_6_out, b1);
  not not_7 (not_7_out, b2);
  not not_8 (not_8_out, b1);
  not not_9 (not_9_out, b3);
  not not_10 (not_10_out, b0);
  not not_11 (not_11_out, b2);
  and and_1 (and_1_out, not_1_out, not_2_out);
  and and_2 (and_2_out, not_3_out, not_4_out, not_5_out);
  and and_3 (and_3_out, not_6_out, not_7_out);
  and and_4 (and_4_out, not_8_out, not_9_out);
  and and_5 (and_5_out, not_10_out, b2, b3);
  and and_6 (and_6_out, b0, not_11_out, b3);
  or or_1 (b, and_1_out, and_2_out, and_3_out, and_4_out, and_5_out, and_6_out);
endmodule

module segc (
  input  b0,
  input  b1,
  input  b2,
  input  b3,
  output c
);

  wire and_1_out, and_2_out, and_3_out, and_4_out, and_5_out, not_1_out, not_2_out, not_3_out, not_4_out,
       not_5_out, not_6_out;

  not not_1 (not_1_out, b0);
  and and_1 (and_1_out, not_1_out, not_2_out);
  not not_2 (not_2_out, b2);
  not not_3 (not_3_out, b0);
  and and_2 (and_2_out, not_3_out, b3);
  not not_4 (not_4_out, b2);
  and and_3 (and_3_out, not_4_out, b3);
  not not_5 (not_5_out, b0);
  and and_4 (and_4_out, not_5_out, b1);
  and and_5 (and_5_out, b0, not_6_out);
  not not_6 (not_6_out, b1);
  or or_1 (c, and_1_out, and_2_out, and_3_out, and_4_out, and_5_out);
endmodule

module segd (
  input  b0,
  input  b1,
  input  b2,
  input  b3,
  output d
);

  wire and_1_out, and_2_out, and_3_out, and_4_out, and_5_out, not_1_out, not_2_out, not_3_out, not_4_out,
       not_5_out, not_6_out, not_7_out;

  not not_1 (not_1_out, b0);
  not not_2 (not_2_out, b1);
  not not_3 (not_3_out, b3);
  not not_4 (not_4_out, b1);
  not not_5 (not_5_out, b2);
  not not_6 (not_6_out, b3);
  not not_7 (not_7_out, b2);
  and and_1 (and_1_out, not_1_out, not_2_out, not_3_out);
  and and_2 (and_2_out, not_4_out, b2, b3);
  and and_3 (and_3_out, b1, not_5_out, b3);
  and and_4 (and_4_out, b1, b2, not_6_out);
  and and_5 (and_5_out, b0, not_7_out);
  or or_1 (d, and_1_out, and_2_out, and_3_out, and_4_out, and_5_out);
endmodule

module sege (
  input  b0,
  input  b1,
  input  b2,
  input  b3,
  output e
);

  wire and_1_out, and_2_out, and_3_out, and_4_out, not_1_out, not_2_out, not_3_out;

  not not_1 (not_1_out, b1);
  and and_1 (and_1_out, not_1_out, not_2_out);
  not not_2 (not_2_out, b3);
  and and_2 (and_2_out, b2, not_3_out);
  not not_3 (not_3_out, b3);
  and and_3 (and_3_out, b0, b2);
  and and_4 (and_4_out, b0, b1);
  or or_1 (e, and_1_out, and_2_out, and_3_out, and_4_out);
endmodule

module segf (
  input  b0,
  input  b1,
  input  b2,
  input  b3,
  output f
);

  wire and_1_out, and_2_out, and_3_out, and_4_out, and_5_out, not_1_out, not_2_out, not_3_out, not_4_out,
       not_5_out, not_6_out;

  not not_1 (not_1_out, b2);
  and and_1 (and_1_out, not_1_out, not_2_out);
  not not_2 (not_2_out, b3);
  not not_3 (not_3_out, b0);
  and and_2 (and_2_out, not_3_out, b1, not_4_out);
  not not_4 (not_4_out, b2);
  and and_3 (and_3_out, b1, not_5_out);
  not not_5 (not_5_out, b3);
  and and_4 (and_4_out, b0, not_6_out);
  not not_6 (not_6_out, b1);
  and and_5 (and_5_out, b0, b2);
  or or_1 (f, and_1_out, and_2_out, and_3_out, and_4_out, and_5_out);
endmodule

module segg (
  input  b0,
  input  b1,
  input  b2,
  input  b3,
  output g
);

  wire and_1_out, and_2_out, and_3_out, and_4_out, and_5_out, not_1_out, not_2_out, not_3_out, not_4_out,
       not_5_out;

  not not_1 (not_1_out, b1);
  and and_1 (and_1_out, not_1_out, b2);
  and and_2 (and_2_out, b2, not_2_out);
  not not_2 (not_2_out, b3);
  not not_3 (not_3_out, b0);
  and and_3 (and_3_out, not_3_out, b1, not_4_out);
  not not_4 (not_4_out, b2);
  and and_4 (and_4_out, b0, not_5_out);
  not not_5 (not_5_out, b1);
  and and_5 (and_5_out, b0, b3);
  or or_1 (g, and_1_out, and_2_out, and_3_out, and_4_out, and_5_out);
endmodule

module countten (
  input  Enable,
  input  Clk,
  output B0,
  output b1,
  output B2,
  output B3,
  output Co
);

  wire and_1_out, and_2_out, and_3_out, and_5_out, and_6_out, and_7_out, not_1_out;

  and and_1 (and_1_out, Enable, B0);
  Clock clock_1 ();  // open: out
  and and_2 (and_2_out, and_1_out, b1);
  and and_3 (and_3_out, and_2_out, B2);
  J_K_Flip_Flop j_k_ff_1 (.J(Enable), .K(Enable), .clk(Clk), .Q(B0), .reset(and_7_out));  // open: Qn, preset
  J_K_Flip_Flop j_k_ff_2 (.J(and_1_out), .K(and_1_out), .clk(Clk), .Q(b1), .reset(and_7_out));  // open: Qn, preset
  J_K_Flip_Flop j_k_ff_3 (.J(and_2_out), .K(and_2_out), .clk(Clk), .Q(B2), .reset(and_7_out));  // open: Qn, preset
  J_K_Flip_Flop j_k_ff_4 (.J(and_3_out), .K(and_3_out), .clk(Clk), .Q(B3), .reset(and_7_out));  // open: Qn, preset
  and and_4 (Co, B3, and_3_out);
  not not_1 (not_1_out, B2);
  and and_5 (and_5_out, B0, not_1_out);
  and and_6 (and_6_out, b1, B3);
  and and_7 (and_7_out, and_5_out, and_6_out);
endmodule

module threebitmodfive (
  input  in_1,
  input  in_2,
  input  in_3,
  output out_4,
  output out_5,
  output out_6
);

  wire and_1_out, j_k_ff_1_qn, j_k_ff_2_qn, not_1_out, or_1_out;

  J_K_Flip_Flop j_k_ff_1 (
    .J(in_2), .K(in_2), .clk(in_3), .Q(out_4), .Qn(j_k_ff_1_qn), .reset(or_1_out));  // open: preset
  J_K_Flip_Flop j_k_ff_2 (
    .J(in_2), .K(in_2), .clk(j_k_ff_1_qn), .Q(out_5), .Qn(j_k_ff_2_qn), .reset(or_1_out));  // open: preset
  not not_1 (not_1_out, out_4);
  J_K_Flip_Flop j_k_ff_3 (.J(in_2), .K(in_2), .clk(j_k_ff_2_qn), .Q(out_6), .reset(or_1_out));  // open: Qn, preset
  and and_1 (and_1_out, out_6, out_5, not_1_out);
  or or_1 (or_1_out, and_1_out, in_1);
endmodule

module twobitmodthree (
  input  in_1,
  input  in_2,
  input  in_3,
  output out_4,
  output out_5
);

  wire and_1_out, j_k_ff_1_qn, or_1_out;

  J_K_Flip_Flop j_k_ff_1 (
    .J(in_2), .K(in_2), .clk(in_3), .Q(out_4), .Qn(j_k_ff_1_qn), .reset(or_1_out));  // open: preset
  J_K_Flip_Flop j_k_ff_2 (.J(in_2), .K(in_2), .clk(j_k_ff_1_qn), .Q(out_5), .reset(or_1_out));  // open: Qn, preset
  and and_1 (and_1_out, out_4, out_5);
  or or_1 (or_1_out, and_1_out, in_1);
endmodule

module \interface  (
  input  in_1,
  input  in_2,
  output [6:0] out_3,
  output [6:0] out_4,
  output [6:0] out_5,
  output [6:0] out_6
);

  wire clockdividerbytwohundred_1_out_2, decoder_1_out0, decoder_1_out1, decoder_1_out2, decoder_1_out3;
  wire [1:0] twobitcountr_1_out_3;
  wire [3:0] hoursmincounter_1_out_2, hoursmincounter_1_out_3, hoursmincounter_1_out_4,
       hoursmincounter_1_out_5;
  wire [6:0] sevenseg_1_out_2, sevenseg_2_out_2, sevenseg_3_out_2, sevenseg_4_out_2;

  twobitcountr twobitcountr_1 (
    .in_2(in_2), .in_1(in_1), .out_3(twobitcountr_1_out_3[0]), .out_4(twobitcountr_1_out_3[1]));
  Decoder #(.select(2)) decoder_1 (
    .out0(decoder_1_out0), .out1(decoder_1_out1), .out2(decoder_1_out2), .out3(decoder_1_out3),
    .sel(twobitcountr_1_out_3), .en(in_1));
  Multiplexer #(.enable("true"), .width(7)) multiplexer_1 (
    .in0({7{1'b0}}), .in1(sevenseg_1_out_2), .out(out_3), .sel(decoder_1_out0), .en(in_1));
  Multiplexer #(.enable("true"), .width(7)) multiplexer_2 (
    .in0({7{1'b0}}), .in1(sevenseg_2_out_2), .out(out_4), .sel(decoder_1_out1), .en(in_1));
  clockdividerbytwohundred clockdividerbytwohundred_1 (.in_1(in_1), .out_2(clockdividerbytwohundred_1_out_2));
  Multiplexer #(.enable("true"), .width(7)) multiplexer_3 (
    .in0({7{1'b0}}), .in1(sevenseg_3_out_2), .out(out_5), .sel(decoder_1_out2), .en(in_1));
  sevenseg sevenseg_1 (.in_1(hoursmincounter_1_out_4), .out_2(sevenseg_1_out_2));
  Multiplexer #(.enable("true"), .width(7)) multiplexer_4 (
    .in0({7{1'b0}}), .in1(sevenseg_4_out_2), .out(out_6), .sel(decoder_1_out3), .en(in_1));
  sevenseg sevenseg_2 (.in_1(hoursmincounter_1_out_2), .out_2(sevenseg_2_out_2));
  hoursmincounter hoursmincounter_1 (
    .in_1(in_1), .out_4(hoursmincounter_1_out_4), .out_2(hoursmincounter_1_out_2),
    .out_3(hoursmincounter_1_out_3), .out_5(hoursmincounter_1_out_5));
  sevenseg sevenseg_3 (.in_1(hoursmincounter_1_out_3), .out_2(sevenseg_3_out_2));
  sevenseg sevenseg_4 (.in_1(hoursmincounter_1_out_5), .out_2(sevenseg_4_out_2));
endmodule

module clockdividerbytwohundred (
  input  in_1,
  output out_2
);

  wire and_1_out, clock_1_out, modulo100counter_1_out_6, modulo100counter_1_out_9, modulo100counter_1_out_10;

  Clock clock_1 (.out(clock_1_out));
  modulo100counter modulo100counter_1 (
    .in_3(clock_1_out), .in_2(in_1), .out_10(modulo100counter_1_out_10), .out_6(modulo100counter_1_out_6),
    .out_9(modulo100counter_1_out_9));  // open: in_1, out_4, out_5, out_7, out_8
  and and_1 (and_1_out, modulo100counter_1_out_6, modulo100counter_1_out_9, modulo100counter_1_out_10);
  T_Flip_Flop t_ff_1 (.T(and_1_out), .clk(clock_1_out), .Q(out_2));  // open: Qn, reset, preset
endmodule

module modulo100counter (
  input  in_1,
  input  in_2,
  input  in_3,
  output out_4,
  output out_5,
  output out_6,
  output out_7,
  output out_8,
  output out_9,
  output out_10
);

  wire and_1_out, j_k_ff_1_qn, j_k_ff_2_qn, j_k_ff_3_qn, j_k_ff_4_qn, j_k_ff_5_qn, j_k_ff_6_qn, or_1_out;

  J_K_Flip_Flop j_k_ff_1 (
    .J(in_2), .K(in_2), .clk(in_3), .Q(out_4), .Qn(j_k_ff_1_qn), .reset(or_1_out));  // open: preset
  J_K_Flip_Flop j_k_ff_2 (
    .J(in_2), .K(in_2), .clk(j_k_ff_1_qn), .Q(out_5), .Qn(j_k_ff_2_qn), .reset(or_1_out));  // open: preset
  J_K_Flip_Flop j_k_ff_3 (
    .J(in_2), .K(in_2), .clk(j_k_ff_2_qn), .Q(out_6), .Qn(j_k_ff_3_qn), .reset(or_1_out));  // open: preset
  J_K_Flip_Flop j_k_ff_4 (
    .J(in_2), .K(in_2), .clk(j_k_ff_3_qn), .Q(out_7), .Qn(j_k_ff_4_qn), .reset(or_1_out));  // open: preset
  J_K_Flip_Flop j_k_ff_5 (
    .J(in_2), .K(in_2), .clk(j_k_ff_4_qn), .Q(out_8), .Qn(j_k_ff_5_qn), .reset(or_1_out));  // open: preset
  J_K_Flip_Flop j_k_ff_6 (
    .J(in_2), .K(in_2), .clk(j_k_ff_5_qn), .Q(out_9), .Qn(j_k_ff_6_qn), .reset(or_1_out));  // open: preset
  J_K_Flip_Flop j_k_ff_7 (.J(in_2), .K(in_2), .clk(j_k_ff_6_qn), .Q(out_10), .reset(or_1_out));  // open: Qn, preset
  and and_1 (and_1_out, out_4, out_6, out_9, out_10);
  or or_1 (or_1_out, and_1_out, in_1);
endmodule

module twobitcountr (
  input  in_1,
  input  in_2,
  output out_3,
  output out_4
);

  wire j_k_ff_1_qn;

  J_K_Flip_Flop j_k_ff_1 (.J(in_1), .K(in_1), .clk(in_2), .Q(out_3), .Qn(j_k_ff_1_qn));  // open: preset, reset
  J_K_Flip_Flop j_k_ff_2 (.J(in_1), .K(in_1), .clk(j_k_ff_1_qn), .Q(out_4));  // open: Qn, preset, reset
endmodule

module mainn (
  input  in_1
);

  wire clock_1_out;
  wire [6:0] interface_1_out_3, interface_1_out_4, interface_1_out_5, interface_1_out_6;

  Clock clock_1 (.out(clock_1_out));
  _7_Segment_Display u_7_segment_display_1 (
    .g(interface_1_out_3[6]), .f(interface_1_out_3[5]), .a(interface_1_out_3[0]), .b(interface_1_out_3[1]),
    .e(interface_1_out_3[4]), .d(interface_1_out_3[3]), .c(interface_1_out_3[2]));  // open: dp
  _7_Segment_Display u_7_segment_display_2 (
    .g(interface_1_out_4[6]), .f(interface_1_out_4[5]), .a(interface_1_out_4[0]), .b(interface_1_out_4[1]),
    .e(interface_1_out_4[4]), .d(interface_1_out_4[3]), .c(interface_1_out_4[2]));  // open: dp
  \interface  interface_1 (
    .in_1(in_1), .in_2(clock_1_out), .out_3(interface_1_out_3), .out_4(interface_1_out_4),
    .out_5(interface_1_out_5), .out_6(interface_1_out_6));
  _7_Segment_Display u_7_segment_display_3 (
    .g(interface_1_out_5[6]), .f(interface_1_out_5[5]), .a(interface_1_out_5[0]), .b(interface_1_out_5[1]),
    .e(interface_1_out_5[4]), .d(interface_1_out_5[3]), .c(interface_1_out_5[2]));  // open: dp
  _7_Segment_Display u_7_segment_display_4 (
    .g(interface_1_out_6[6]), .f(interface_1_out_6[5]), .a(interface_1_out_6[0]), .b(interface_1_out_6[1]),
    .e(interface_1_out_6[4]), .d(interface_1_out_6[3]), .c(interface_1_out_6[2]));  // open: dp
endmodule
